# Fritzing sketch schema (saved by Fritzing 0.9.3b)
circuit board: 8.46667cm x 5.64444cm
breadboards: 1

parts:
  Part1 = Arduino Uno (Rev3) - ICSP
  IR1 = TSOP312.., 314.. [package=THT]
  LED1 = LED - 5mm [color="Red (633nm)" package="5 mm [THT]"]
  R1 = Resistor [tolerance=±5% resistance=220 package=THT]

nets:
  N1: Part1.5V, IR1.Vs
  GND: Part1.GND, IR1.GND, LED1.cathode
  N2: Part1.D8, R1.Pin_1
  N3: Part1.D5_PWM, IR1.Data
  N4: LED1.anode, R1.Pin_0
