# Fritzing sketch schema (saved by Fritzing 0.9.3b)
circuit board: 8.46667cm x 5.64444cm
breadboards: 1

parts:
  Part1 = Arduino Uno (Rev3) - ICSP
  LED1 = LED - 5mm [color="Red (633nm)" package="5 mm [THT]"]
  IR1 = TSOP312.., 314.. [package=THT]

nets:
  N1: Part1.5V, IR1.Vs
  GND: Part1.GND, LED1.cathode, IR1.GND
  N2: Part1.D4, LED1.anode
  N3: Part1.D5_PWM, IR1.Data
